# Fritzing sketch PCB (saved by Fritzing 1.0.1rc)
circuit board: 3.2cm x 5.07068cm

parts:
  J9 = female pin header, 4 pins [form="♀ (female)"]
  J10 = female pin header, 4 pins [form="♀ (female)"]
  J6 = double row female pin header, 10 pins [form="♀ (female)"]
  J11 = female pin header, 2 pins [form="♀ (female)"]
  J7 = female pin header, 1 pin [form="♀ (female)"]
  J12 = female pin header, 5 pins [form="♀ (female)"]  # not connected
  J13 = female pin header, 10 pins [form="♀ (female)"]  # not connected
  J8 = female pin header, 2 pins [form="♀ (female)"]

nets:
  N1: J9.pin1, J6.pin6
  N2: J9.pin2, J6.pin7
  N3: J9.pin3, J6.pin8
  N4: J9.pin4, J6.pin9
  N5: J10.pin1, J6.pin5
  N6: J10.pin2, J6.pin4
  N7: J10.pin3, J6.pin3
  N8: J10.pin4, J6.pin2
  N9: J6.pin1, J7.pin1
  N10: J11.pin1, J11.pin2, J8.pin1

notes:
  12
  14
  27
  15
  2
  0
  4
  STEP
  DIR
  X
  Y
  Z
  A
  5V
  GND
  EN
  26
  CNC V3 ESP-WROOM-32
