# Fritzing sketch PCB (saved by Fritzing 1.0.1rc)
circuit board: 3.49752cm x 6.27475cm

parts:
  J1 = female pin header, 5 pins [form="♀ (female)"]
  J2 = female pin header, 5 pins [form="♀ (female)"]
  U1 = ESP32S-HiLetgo [part_number=ESP32S-HiLetgo]

nets:
  N1: J1.pin2, U1.GPIO26
  N2: J1.pin3, U1.GPIO27
  N3: J1.pin4, U1.GPIO14
  N4: J1.pin5, U1.GPIO12
  N5: J2.pin1, U1.GPIO15
  N6: J2.pin2, U1.GPIO2
  N7: J2.pin3, U1.GPIO0
  N8: J2.pin4, U1.GPIO4
  N9: J2.pin5, U1.GND

notes:
  12 A Step
  14 Z Step
  27 Y Step
  15 X Dir
  2 Y Dir
  0 Z Dir
  4 A Dir
  X Y Z A
  26 X Step
  CNC V3 ESP-WROOM-32

custom parts:
  ESP32S-HiLetgo: HiLetgo ESP-WROOM-32 ESP32 ESP-32S Development Board 2.4GHz Dual-Mode WiFi + Bluetooth Dual Cores Microcontroller The ESP32 integrated with Antenna switches, RF Balun, power amplifiers, low-noise amplifiers, filters, and management modules, and the entire solution occupies the least area of PCB. 2.4 GHz Wi-Fi plus Bluetooth dual-mode chip, with TSMC Ultra-low power consumption 40nm technology,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
